// Logisim project componente_1_Flip-flop.circ as structural Verilog: 2 circuits, main circuit main
module main (
  input  preset,
  input  entrada,
  input  clock,
  input  clear,
  output out_5,
  output out_6
);

  wire nand_1_out, nand_2_out, nand_3_out, nand_4_out, nand_5_out, nand_6_out, not_1_out, not_2_out,
       not_3_out, not_4_out;

  not not_1 (not_1_out, entrada);
  nand nand_1 (nand_1_out, entrada, clock);
  nand nand_2 (nand_2_out, clock, not_1_out);
  not not_2 (not_2_out, clock);
  nand nand_3 (nand_3_out, not_3_out, nand_1_out, nand_4_out);
  nand nand_4 (nand_4_out, nand_3_out, nand_2_out, not_4_out);
  not not_3 (not_3_out, preset);
  nand nand_5 (nand_5_out, nand_3_out, not_4_out, not_2_out);
  nand nand_6 (nand_6_out, not_2_out, not_2_out, not_3_out, nand_4_out);
  not not_4 (not_4_out, clear);
  nand nand_7 (out_5, nand_5_out, not_3_out, out_6);
  nand nand_8 (out_6, out_5, not_4_out, nand_6_out);

  // Notes on the sheet:
  //   FLIP FLOP TIPO D
endmodule

module flip_flop_jk (
  input  J,
  input  R,
  input  clear,
  input  preset,
  output Q,
  output nQ
);

  wire and_1_out, and_2_out, clock_1_out, not_1_out, or_1_out;

  Clock clock_1 (.out(clock_1_out));
  and and_1 (and_1_out, J, nQ);
  not not_1 (not_1_out, R);
  and and_2 (and_2_out, not_1_out, Q);
  or or_1 (or_1_out, and_1_out, and_2_out);
  main main_1 (.entrada(or_1_out), .preset(preset), .clock(clock_1_out), .clear(clear), .out_5(Q), .out_6(nQ));

  // Notes on the sheet:
  //   Flip flop JK
endmodule
