// Logisim project Componente10_ULA.circ as structural Verilog: 17 circuits, main circuit main
module main (
  input  [7:0] Entrada_A,
  input  [7:0] Entrada_B,
  input  [3:0] Seletor,
  output [7:0] \Saída 
);

  ULA ula_1 (.entrada_A(Entrada_A), .entrada_B(Entrada_B), .in_3(Seletor), .out_4(\Saída ));

  // Notes on the sheet:
  //   0000 - AND
  //   0001 - OR
  //   0010 - NOT A
  //   0011 - NOT B
  //   0100 - NOR
  //   0101 - NAND
  //   0110 - XOR
  //   1011 - Soma
  //   1100 - Subtração
  //   0111 - SHIFT A 2 bits para a esquerda
  //   1000 - SHIFT B 2 bits para a esquerda
  //   1001 - SHIFT A 1 bit para a direita
  //   1010 - SHIFT B 1 bit para a direita
endmodule

module Flip_FLop_D (
  input  Data,
  input  in_2,
  output Q,
  output nQ
);

  wire nand_1_out, nand_2_out;

  nand nand_1 (nand_1_out, in_2, ~Data);  // NAND_Gate
  nand nand_2 (nand_2_out, Data, in_2);
  nand nand_3 (Q, nand_2_out, nQ);
  nand nand_4 (nQ, Q, nand_1_out);
endmodule

module Flip_Flop_JK (
  input  Clock_Enable,
  input  J,
  input  K,
  output out_4,
  output out_5
);

  wire and_1_out, and_2_out, or_1_out;

  and and_1 (and_1_out, J, out_5);
  or or_1 (or_1_out, and_1_out, and_2_out);
  and and_2 (and_2_out, out_4, ~K);  // AND_Gate
  D_Flip_Flop d_ff_1 (.clk(Clock_Enable), .D(or_1_out), .Q(out_4), .Qn(out_5));  // open: preset, en, reset
endmodule

module Multiplexador_4_bits (
  input  [3:0] Seletor_4_bits,
  output _0,
  output _1,
  output _2,
  output _3,
  output _4,
  output _5,
  output _6,
  output _7,
  output _8,
  output _9,
  output _10,
  output _11,
  output _12
);

  and and_1 (_0, ~Seletor_4_bits[0], ~Seletor_4_bits[1], ~Seletor_4_bits[2], ~Seletor_4_bits[3]);  // AND_Gate
  and and_2 (_1, Seletor_4_bits[0], ~Seletor_4_bits[1], ~Seletor_4_bits[2], ~Seletor_4_bits[3]);  // AND_Gate
  and and_3 (_2, ~Seletor_4_bits[0], Seletor_4_bits[1], ~Seletor_4_bits[2], ~Seletor_4_bits[3]);  // AND_Gate
  and and_4 (_3, Seletor_4_bits[0], Seletor_4_bits[1], ~Seletor_4_bits[2], ~Seletor_4_bits[3]);  // AND_Gate
  and and_5 (_4, ~Seletor_4_bits[0], ~Seletor_4_bits[1], Seletor_4_bits[2], ~Seletor_4_bits[3]);  // AND_Gate
  and and_6 (_5, Seletor_4_bits[0], ~Seletor_4_bits[1], Seletor_4_bits[2], ~Seletor_4_bits[3]);  // AND_Gate
  and and_7 (_6, ~Seletor_4_bits[0], Seletor_4_bits[1], Seletor_4_bits[2], ~Seletor_4_bits[3]);  // AND_Gate
  and and_8 (_7, ~Seletor_4_bits[3], Seletor_4_bits[2], Seletor_4_bits[1], Seletor_4_bits[0]);  // AND_Gate
  and and_9 (_8, ~Seletor_4_bits[0], ~Seletor_4_bits[1], ~Seletor_4_bits[2], Seletor_4_bits[3]);  // AND_Gate
  and and_10 (_9, Seletor_4_bits[3], ~Seletor_4_bits[2], ~Seletor_4_bits[1], Seletor_4_bits[0]);  // AND_Gate
  and and_11 (_10, Seletor_4_bits[3], ~Seletor_4_bits[2], Seletor_4_bits[1], ~Seletor_4_bits[0]);  // AND_Gate
  and and_12 (_11, Seletor_4_bits[3], Seletor_4_bits[0], Seletor_4_bits[1], ~Seletor_4_bits[2]);  // AND_Gate
  and and_13 (_12, Seletor_4_bits[3], Seletor_4_bits[2], ~Seletor_4_bits[1], ~Seletor_4_bits[0]);  // AND_Gate
endmodule

module AND (
  input  [7:0] in_1,
  input  [7:0] in_2,
  output [7:0] out_3
);

  assign out_3 = in_1 & in_2;  // AND_Gate and_1, 8 bits wide
endmodule

module OR (
  input  [7:0] in_1,
  input  [7:0] in_2,
  output [7:0] out_3
);

  assign out_3 = in_1 | in_2;  // OR_Gate or_1, 8 bits wide
endmodule

module NOT (
  input  [7:0] in_1,
  output [7:0] out_2
);

  assign out_2 = ~in_1;  // NOT_Gate not_1, 8 bits wide
endmodule

module NOR (
  input  [7:0] in_1,
  input  [7:0] in_2,
  output [7:0] out_3
);

  assign out_3 = ~(in_1 | in_2);  // NOR_Gate nor_1, 8 bits wide
endmodule

module NAND (
  input  [7:0] in_1,
  input  [7:0] in_2,
  output [7:0] out_3
);

  assign out_3 = ~(in_1 & in_2);  // NAND_Gate nand_1, 8 bits wide
endmodule

module ULA (
  input  [7:0] entrada_A,
  input  [7:0] entrada_B,
  input  [3:0] in_3,
  output [7:0] out_4
);

  wire multiplexador_4_bits_1__0, multiplexador_4_bits_1__1, multiplexador_4_bits_1__2,
       multiplexador_4_bits_1__3, multiplexador_4_bits_1__4, multiplexador_4_bits_1__5,
       multiplexador_4_bits_1__6, multiplexador_4_bits_1__7, multiplexador_4_bits_1__8,
       multiplexador_4_bits_1__9, multiplexador_4_bits_1__10, multiplexador_4_bits_1__11,
       multiplexador_4_bits_1__12;
  wire [7:0] and_1_out_3, deslocador_direita_1_out_2, deslocador_direita_2_out_2,
       deslocador_esquerda_1_bit_deslocado, deslocador_esquerda_2_bit_deslocado, nand_1_out_3, nor_1_out_3,
       not_1_out_2, NOT_B_out_2, or_1_out_3, somador_8_bits_1_out_3, subtrator_8_bits_1_out_3, xor_1_out_3;

  Multiplexador_4_bits multiplexador_4_bits_1 (
    .Seletor_4_bits(in_3), ._0(multiplexador_4_bits_1__0), ._1(multiplexador_4_bits_1__1),
    ._2(multiplexador_4_bits_1__2), ._3(multiplexador_4_bits_1__3), ._4(multiplexador_4_bits_1__4),
    ._5(multiplexador_4_bits_1__5), ._6(multiplexador_4_bits_1__6), ._7(multiplexador_4_bits_1__7),
    ._8(multiplexador_4_bits_1__8), ._9(multiplexador_4_bits_1__9), ._10(multiplexador_4_bits_1__10),
    ._11(multiplexador_4_bits_1__11), ._12(multiplexador_4_bits_1__12));
  AND and_1 (.in_1(entrada_A), .in_2(entrada_B), .out_3(and_1_out_3));
  OR or_1 (.in_1(entrada_A), .in_2(entrada_B), .out_3(or_1_out_3));
  NOT not_1 (.in_1(entrada_A), .out_2(not_1_out_2));
  NOT NOT_B (.in_1(entrada_B), .out_2(NOT_B_out_2));
  NOR nor_1 (.in_1(entrada_A), .in_2(entrada_B), .out_3(nor_1_out_3));
  NAND nand_1 (.in_1(entrada_A), .in_2(entrada_B), .out_3(nand_1_out_3));
  XOR xor_1 (.in_1(entrada_A), .in_2(entrada_B), .out_3(xor_1_out_3));
  Deslocador_Esquerda deslocador_esquerda_1 (.entrada(entrada_A), .bit_deslocado(deslocador_esquerda_1_bit_deslocado));
  Deslocador_Esquerda deslocador_esquerda_2 (.entrada(entrada_B), .bit_deslocado(deslocador_esquerda_2_bit_deslocado));
  Deslocador_Direita deslocador_direita_1 (.in_1(entrada_A), .out_2(deslocador_direita_1_out_2));
  Deslocador_Direita deslocador_direita_2 (.in_1(entrada_B), .out_2(deslocador_direita_2_out_2));
  Somador_8_bits somador_8_bits_1 (.in_1(entrada_A), .Entrada_B(entrada_B), .out_3(somador_8_bits_1_out_3));
  Subtrator_8_bits subtrator_8_bits_1 (.in_1(entrada_A), .Entrada_B(entrada_B), .out_3(subtrator_8_bits_1_out_3));
  assign out_4 = multiplexador_4_bits_1__0 ? and_1_out_3 : 8'bz;  // Controlled_Buffer controlled_buffer_1
  assign out_4 = multiplexador_4_bits_1__1 ? or_1_out_3 : 8'bz;  // Controlled_Buffer controlled_buffer_2
  assign out_4 = multiplexador_4_bits_1__2 ? not_1_out_2 : 8'bz;  // Controlled_Buffer controlled_buffer_3
  assign out_4 = multiplexador_4_bits_1__3 ? NOT_B_out_2 : 8'bz;  // Controlled_Buffer controlled_buffer_4
  assign out_4 = multiplexador_4_bits_1__4 ? nor_1_out_3 : 8'bz;  // Controlled_Buffer controlled_buffer_5
  assign out_4 = multiplexador_4_bits_1__5 ? nand_1_out_3 : 8'bz;  // Controlled_Buffer controlled_buffer_6
  assign out_4 = multiplexador_4_bits_1__6 ? xor_1_out_3 : 8'bz;  // Controlled_Buffer controlled_buffer_7
  assign out_4 = multiplexador_4_bits_1__7 ? deslocador_esquerda_1_bit_deslocado : 8'bz;  // Controlled_Buffer controlled_buffer_8
  assign out_4 = multiplexador_4_bits_1__8 ? deslocador_esquerda_2_bit_deslocado : 8'bz;  // Controlled_Buffer controlled_buffer_9
  assign out_4 = multiplexador_4_bits_1__9 ? deslocador_direita_1_out_2 : 8'bz;  // Controlled_Buffer controlled_buffer_10
  assign out_4 = multiplexador_4_bits_1__10 ? deslocador_direita_2_out_2 : 8'bz;  // Controlled_Buffer controlled_buffer_11
  assign out_4 = multiplexador_4_bits_1__11 ? somador_8_bits_1_out_3 : 8'bz;  // Controlled_Buffer controlled_buffer_12
  assign out_4 = multiplexador_4_bits_1__12 ? subtrator_8_bits_1_out_3 : 8'bz;  // Controlled_Buffer controlled_buffer_13

  // Notes on the sheet:
  //   NOT A
  //   << A
  //   << B
  //   >> A
  //   >> B
  //   soma
  //   sub
endmodule

module XOR (
  input  [7:0] in_1,
  input  [7:0] in_2,
  output [7:0] out_3
);

  assign out_3 = in_1 ^ in_2;  // XOR_Gate xor_1, 8 bits wide
endmodule

module Deslocador_Esquerda (
  input  [7:0] entrada,
  output [7:0] bit_deslocado
);


  assign bit_deslocado = {entrada[5:0], 2'b00};
  assign entrada[6] = entrada[7];
  // also tied to GND on the sheet: entrada[7]
endmodule

module Deslocador_Direita (
  input  [7:0] in_1,
  output [7:0] out_2
);


  assign out_2 = {1'b0, in_1[7:1]};
  // also tied to GND on the sheet: in_1[0]
endmodule

module Somador (
  input  A,
  input  B,
  input  Carry_in,
  output \Saída ,
  output Carry_Out
);

  wire and_1_out, and_2_out, or_1_out, xor_1_out;

  xor xor_1 (xor_1_out, A, B);
  and and_1 (and_1_out, B, A);
  and and_2 (and_2_out, Carry_in, or_1_out);
  or or_1 (or_1_out, B, A);
  xor xor_2 (\Saída , xor_1_out, Carry_in);
  or or_2 (Carry_Out, and_1_out, and_2_out);
endmodule

module Somador_8_bits (
  input  [7:0] in_1,
  input  [7:0] Entrada_B,
  output [7:0] out_3
);

  wire somador_1_carry_out, somador_2_carry_out, somador_3_carry_out, somador_4_carry_out,
       somador_5_carry_out, somador_6_carry_out, somador_7_carry_out, somador_8_carry_out;

  Somador somador_1 (
    .A(in_1[0]), .\Saída (out_3[0]), .B(Entrada_B[0]), .Carry_Out(somador_1_carry_out), .Carry_in(1'b0));
  Somador somador_2 (
    .A(in_1[1]), .\Saída (out_3[1]), .B(Entrada_B[1]), .Carry_Out(somador_2_carry_out),
    .Carry_in(somador_1_carry_out));
  Somador somador_3 (
    .A(in_1[2]), .\Saída (out_3[2]), .B(Entrada_B[2]), .Carry_Out(somador_3_carry_out),
    .Carry_in(somador_2_carry_out));
  Somador somador_4 (
    .A(in_1[4]), .\Saída (out_3[4]), .B(Entrada_B[4]), .Carry_Out(somador_4_carry_out),
    .Carry_in(somador_5_carry_out));
  Somador somador_5 (
    .A(in_1[3]), .\Saída (out_3[3]), .B(Entrada_B[3]), .Carry_Out(somador_5_carry_out),
    .Carry_in(somador_3_carry_out));
  Somador somador_6 (
    .A(in_1[5]), .\Saída (out_3[5]), .B(Entrada_B[5]), .Carry_Out(somador_6_carry_out),
    .Carry_in(somador_4_carry_out));
  Somador somador_7 (
    .A(in_1[6]), .\Saída (out_3[6]), .B(Entrada_B[6]), .Carry_Out(somador_7_carry_out),
    .Carry_in(somador_6_carry_out));
  Somador somador_8 (
    .A(in_1[7]), .\Saída (out_3[7]), .B(Entrada_B[7]), .Carry_Out(somador_8_carry_out),
    .Carry_in(somador_7_carry_out));
  // also tied to GND on the sheet: somador_8_carry_out

  // Notes on the sheet:
  //   Entrada A
endmodule

module Subtrator (
  input  A,
  input  B,
  input  Empresta,
  output \Saída ,
  output Empresta_Fora
);

  wire and_1_out, and_2_out, and_3_out, not_1_out, xor_1_out;

  xor xor_1 (xor_1_out, A, B);
  not not_1 (not_1_out, A);
  and and_1 (and_1_out, not_1_out, B);
  and and_2 (and_2_out, not_1_out, Empresta);
  and and_3 (and_3_out, B, Empresta);
  xor xor_2 (\Saída , xor_1_out, Empresta);
  or or_1 (Empresta_Fora, and_1_out, and_2_out, and_3_out);
endmodule

module Subtrator_8_bits (
  input  [7:0] in_1,
  input  [7:0] Entrada_B,
  output [7:0] out_3
);

  wire subtrator_1_empresta_fora, subtrator_2_empresta_fora, subtrator_3_empresta_fora,
       subtrator_4_empresta_fora, subtrator_5_empresta_fora, subtrator_6_empresta_fora,
       subtrator_7_empresta_fora, subtrator_8_empresta_fora;

  Subtrator subtrator_1 (
    .A(in_1[0]), .B(Entrada_B[0]), .Empresta(1'b0), .\Saída (out_3[0]),
    .Empresta_Fora(subtrator_1_empresta_fora));
  Subtrator subtrator_2 (
    .A(in_1[1]), .B(Entrada_B[1]), .Empresta(subtrator_1_empresta_fora), .\Saída (out_3[1]),
    .Empresta_Fora(subtrator_2_empresta_fora));
  Subtrator subtrator_3 (
    .A(in_1[2]), .B(Entrada_B[2]), .Empresta(subtrator_2_empresta_fora), .\Saída (out_3[2]),
    .Empresta_Fora(subtrator_3_empresta_fora));
  Subtrator subtrator_4 (
    .A(in_1[3]), .B(Entrada_B[3]), .Empresta(subtrator_3_empresta_fora), .\Saída (out_3[3]),
    .Empresta_Fora(subtrator_4_empresta_fora));
  Subtrator subtrator_5 (
    .A(in_1[4]), .B(Entrada_B[4]), .Empresta(subtrator_4_empresta_fora), .\Saída (out_3[4]),
    .Empresta_Fora(subtrator_5_empresta_fora));
  Subtrator subtrator_6 (
    .A(in_1[5]), .B(Entrada_B[5]), .Empresta(subtrator_5_empresta_fora), .\Saída (out_3[5]),
    .Empresta_Fora(subtrator_6_empresta_fora));
  Subtrator subtrator_7 (
    .A(in_1[6]), .B(Entrada_B[6]), .Empresta(subtrator_6_empresta_fora), .\Saída (out_3[6]),
    .Empresta_Fora(subtrator_7_empresta_fora));
  Subtrator subtrator_8 (
    .A(in_1[7]), .B(Entrada_B[7]), .Empresta(subtrator_7_empresta_fora), .\Saída (out_3[7]),
    .Empresta_Fora(subtrator_8_empresta_fora));
  // also tied to GND on the sheet: subtrator_8_empresta_fora

  // Notes on the sheet:
  //   Entrada A
endmodule
