// Logisim project Componente12_Maquina de estados.circ as structural Verilog: 1 circuit, main circuit main
module main (
  input  Preset,
  input  J,
  input  K,
  input  Clear,
  output out_5,
  output out_6
);

  wire clock_1_out, nand_1_out, nand_2_out, nand_3_out, nand_4_out, nand_5_out, nand_6_out, not_1_out,
       not_2_out, not_3_out;

  Clock clock_1 (.out(clock_1_out));
  nand nand_1 (nand_1_out, out_6, J, clock_1_out);
  not not_1 (not_1_out, clock_1_out);
  nand nand_2 (nand_2_out, clock_1_out, K, out_5);
  not not_2 (not_2_out, Preset);
  not not_3 (not_3_out, Clear);
  nand nand_3 (nand_3_out, not_2_out, nand_1_out, nand_4_out);
  nand nand_4 (nand_4_out, nand_3_out, nand_2_out, not_3_out);
  nand nand_5 (nand_5_out, not_3_out, nand_3_out, not_1_out);
  nand nand_6 (nand_6_out, not_1_out, nand_4_out, not_2_out);
  nand nand_7 (out_5, not_2_out, nand_5_out, out_6);
  nand nand_8 (out_6, out_5, nand_6_out, not_3_out);
endmodule
