// Logisim project componente_13_contador-sincr.circ as structural Verilog: 2 circuits, main circuit main
module main (
  input  preset,
  input  clear,
  output out_3,
  output out_4,
  output out_5,
  output out_6
);

  wire and_1_out, and_2_out, clock_1_out, not_1_out, xor_1_out, xor_2_out, xor_3_out;

  and and_1 (and_1_out, out_3, out_4);
  and and_2 (and_2_out, and_1_out, out_5);
  not not_1 (not_1_out, out_3);
  xor xor_1 (xor_1_out, out_4, out_3);
  xor xor_2 (xor_2_out, out_5, and_1_out);
  xor xor_3 (xor_3_out, out_6, and_2_out);
  Clock clock_1 (.out(clock_1_out));
  flip_flop_d flip_flop_d_1 (
    .entrada(not_1_out), .clock(clock_1_out), .preset(preset), .clear(clear), .out_5(out_3));  // open: out_6
  flip_flop_d flip_flop_d_2 (
    .entrada(xor_1_out), .clock(clock_1_out), .preset(preset), .clear(clear), .out_5(out_4));  // open: out_6
  flip_flop_d flip_flop_d_3 (
    .entrada(xor_2_out), .clock(clock_1_out), .preset(preset), .clear(clear), .out_5(out_5));  // open: out_6
  flip_flop_d flip_flop_d_4 (
    .entrada(xor_3_out), .clock(clock_1_out), .preset(preset), .clear(clear), .out_5(out_6));  // open: out_6
endmodule

module flip_flop_d (
  input  preset,
  input  entrada,
  input  clock,
  input  clear,
  output out_5,
  output out_6
);

  wire nand_1_out, nand_2_out, nand_3_out, nand_4_out, nand_5_out, nand_6_out, not_1_out, not_2_out,
       not_3_out, not_4_out;

  not not_1 (not_1_out, entrada);
  nand nand_1 (nand_1_out, entrada, clock);
  nand nand_2 (nand_2_out, clock, not_1_out);
  not not_2 (not_2_out, clock);
  nand nand_3 (nand_3_out, not_3_out, nand_1_out, nand_4_out);
  nand nand_4 (nand_4_out, nand_3_out, nand_2_out, not_4_out);
  not not_3 (not_3_out, preset);
  nand nand_5 (nand_5_out, nand_3_out, not_4_out, not_2_out);
  nand nand_6 (nand_6_out, not_2_out, not_2_out, not_3_out, nand_4_out);
  not not_4 (not_4_out, clear);
  nand nand_7 (out_5, nand_5_out, not_3_out, out_6);
  nand nand_8 (out_6, out_5, not_4_out, nand_6_out);
endmodule
