// Logisim project componente_14_impar.circ as structural Verilog: 2 circuits, main circuit main
module main (
  input  [3:0] in_1,
  output out_2
);

  wire xor_1_saida, xor_2_saida;

  XOR xor_1 (.A(in_1[0]), .B(in_1[1]), .saida(xor_1_saida));
  XOR xor_2 (.A(xor_1_saida), .B(in_1[2]), .saida(xor_2_saida));
  XOR xor_3 (.A(xor_2_saida), .B(in_1[3]), .saida(out_2));
endmodule

module XOR (
  input  A,
  input  B,
  output saida
);

  wire and_1_out, and_2_out, not_1_out, not_2_out;

  not not_1 (not_1_out, B);
  not not_2 (not_2_out, A);
  and and_1 (and_1_out, A, not_1_out);
  and and_2 (and_2_out, not_2_out, B);
  or or_1 (saida, and_1_out, and_2_out);
endmodule
