// Logisim project Componente15_Problema de otimização lógica.circ as structural Verilog: 1 circuit, main circuit main
module main (
  input  A,
  input  B,
  input  Carry_in,
  input  A_2,
  input  B_2,
  input  Carry_in_2,
  output out_7,
  output S,
  output out_9,
  output Carry_out
);

  wire and_1_out, and_2_out, and_3_out, and_4_out, and_5_out, and_6_out, and_7_out, and_8_out, and_9_out,
       and_10_out, and_11_out, not_1_out, not_2_out, not_3_out, xor_1_out;

  not not_1 (not_1_out, A);
  not not_2 (not_2_out, B);
  not not_3 (not_3_out, Carry_in);
  and and_1 (and_1_out, not_1_out, not_2_out, Carry_in);
  and and_2 (and_2_out, not_1_out, B, not_3_out);
  and and_3 (and_3_out, A, not_2_out, not_3_out);
  and and_4 (and_4_out, A, B, Carry_in);
  and and_5 (and_5_out, not_1_out, B, Carry_in);
  and and_6 (and_6_out, A, not_2_out, Carry_in);
  and and_7 (and_7_out, A, B, not_3_out);
  and and_8 (and_8_out, A, B, Carry_in);
  or or_1 (S, and_1_out, and_2_out, and_3_out, and_4_out);
  or or_2 (Carry_out, and_5_out, and_6_out, and_7_out, and_8_out);
  xor xor_1 (xor_1_out, B_2, A_2);
  xor xor_2 (out_7, xor_1_out, Carry_in_2);
  and and_9 (and_9_out, A_2, B_2);
  and and_10 (and_10_out, Carry_in_2, B_2);
  and and_11 (and_11_out, Carry_in_2, A_2);
  or or_3 (out_9, and_9_out, and_10_out, and_11_out);

  // Notes on the sheet:
  //   Somador completo não otimizado
  //   Somador completo otimizado
endmodule
