// Logisim project componente_16_display_de_7_segmentos.circ as structural Verilog: 8 circuits, main circuit main
module main (
  input  [3:0] in_1
);

  wire a_x, b_x, c_x, d_x, e_x, f_x, g_x;

  saida_a a (.A(in_1[3]), .B(in_1[2]), .C(in_1[1]), .x(a_x), .D(in_1[0]));
  saida_b b (.A(in_1[3]), .B(in_1[2]), .C(in_1[1]), .x(b_x), .D(in_1[0]));
  saida_c c (.A(in_1[3]), .B(in_1[2]), .C(in_1[1]), .x(c_x), .D(in_1[0]));
  saida_d d (.A(in_1[3]), .B(in_1[2]), .C(in_1[1]), .x(d_x), .D(in_1[0]));
  saida_e e (.A(in_1[3]), .B(in_1[2]), .x(e_x), .C(in_1[1]), .D(in_1[0]));
  saida_f f (.A(in_1[3]), .B(in_1[2]), .C(in_1[1]), .x(f_x), .D(in_1[0]));
  saida_g g (.A(in_1[3]), .B(in_1[2]), .C(in_1[1]), .x(g_x), .D(in_1[0]));
  _7_Segment_Display u_7_segment_display_1 (.g(g_x), .f(f_x), .a(a_x), .b(b_x), .e(e_x), .d(d_x), .c(c_x));  // open: dp
endmodule

module saida_a (
  input  A,
  input  B,
  input  C,
  input  D,
  output x
);

  wire and_1_out, and_2_out, and_3_out, and_4_out, and_5_out, and_6_out, not_1_out, not_2_out, not_3_out,
       not_4_out, not_5_out, not_6_out, not_7_out;

  not not_1 (not_1_out, B);
  and and_1 (and_1_out, not_1_out, not_2_out);
  not not_2 (not_2_out, D);
  not not_3 (not_3_out, A);
  and and_2 (and_2_out, not_3_out, C);
  not not_4 (not_4_out, A);
  and and_3 (and_3_out, not_4_out, B, D);
  and and_4 (and_4_out, B, C);
  not not_5 (not_5_out, B);
  and and_5 (and_5_out, A, not_5_out, not_6_out);
  not not_6 (not_6_out, C);
  and and_6 (and_6_out, A, not_7_out);
  not not_7 (not_7_out, D);
  or or_1 (x, and_1_out, and_2_out, and_3_out, and_4_out, and_5_out, and_6_out);
endmodule

module saida_b (
  input  A,
  input  B,
  input  C,
  input  D,
  output x
);

  wire and_1_out, and_2_out, and_3_out, and_4_out, and_5_out, not_1_out, not_2_out, not_3_out, not_4_out,
       not_5_out, not_6_out, not_7_out, not_8_out, not_9_out;

  not not_1 (not_1_out, A);
  and and_1 (and_1_out, not_1_out, not_2_out);
  not not_2 (not_2_out, B);
  not not_3 (not_3_out, A);
  and and_2 (and_2_out, not_3_out, not_4_out, not_5_out);
  not not_4 (not_4_out, C);
  not not_5 (not_5_out, D);
  not not_6 (not_6_out, B);
  and and_3 (and_3_out, not_6_out, not_7_out);
  not not_7 (not_7_out, D);
  not not_8 (not_8_out, A);
  and and_4 (and_4_out, not_8_out, C, D);
  not not_9 (not_9_out, C);
  and and_5 (and_5_out, A, not_9_out, D);
  or or_1 (x, and_1_out, and_2_out, and_3_out, and_4_out, and_5_out);
endmodule

module saida_c (
  input  A,
  input  B,
  input  C,
  input  D,
  output x
);

  wire and_1_out, and_2_out, and_3_out, and_4_out, and_5_out, not_1_out, not_2_out, not_3_out, not_4_out,
       not_5_out, not_6_out;

  not not_1 (not_1_out, A);
  and and_1 (and_1_out, not_1_out, not_2_out);
  not not_2 (not_2_out, C);
  not not_3 (not_3_out, A);
  and and_2 (and_2_out, not_3_out, D);
  not not_4 (not_4_out, C);
  and and_3 (and_3_out, not_4_out, D);
  not not_5 (not_5_out, A);
  and and_4 (and_4_out, not_5_out, B);
  and and_5 (and_5_out, A, not_6_out);
  not not_6 (not_6_out, B);
  or or_1 (x, and_1_out, and_2_out, and_3_out, and_4_out, and_5_out);
endmodule

module saida_d (
  input  A,
  input  B,
  input  C,
  input  D,
  output x
);

  wire and_1_out, and_2_out, and_3_out, and_4_out, and_5_out, not_1_out, not_2_out, not_3_out, not_4_out,
       not_5_out, not_6_out, not_7_out;

  not not_1 (not_1_out, A);
  and and_1 (and_1_out, not_1_out, not_2_out, not_3_out);
  not not_2 (not_2_out, B);
  not not_3 (not_3_out, D);
  not not_4 (not_4_out, B);
  and and_2 (and_2_out, not_4_out, C, D);
  not not_5 (not_5_out, C);
  and and_3 (and_3_out, B, not_5_out, D);
  and and_4 (and_4_out, B, C, not_6_out);
  not not_6 (not_6_out, D);
  and and_5 (and_5_out, A, not_7_out);
  not not_7 (not_7_out, C);
  or or_1 (x, and_1_out, and_2_out, and_3_out, and_4_out, and_5_out);
endmodule

module saida_e (
  input  A,
  input  B,
  input  C,
  input  D,
  output x
);

  wire and_1_out, and_2_out, and_3_out, and_4_out, not_1_out, not_2_out, not_3_out;

  not not_1 (not_1_out, B);
  and and_1 (and_1_out, not_1_out, not_2_out);
  not not_2 (not_2_out, D);
  and and_2 (and_2_out, C, not_3_out);
  not not_3 (not_3_out, D);
  and and_3 (and_3_out, A, C);
  and and_4 (and_4_out, A, B);
  or or_1 (x, and_1_out, and_2_out, and_3_out, and_4_out);
endmodule

module saida_f (
  input  A,
  input  B,
  input  C,
  input  D,
  output x
);

  wire and_1_out, and_2_out, and_3_out, and_4_out, and_5_out, not_1_out, not_2_out, not_3_out, not_4_out,
       not_5_out, not_6_out;

  not not_1 (not_1_out, C);
  and and_1 (and_1_out, not_1_out, not_2_out);
  not not_2 (not_2_out, D);
  not not_3 (not_3_out, A);
  and and_2 (and_2_out, not_3_out, B, not_4_out);
  not not_4 (not_4_out, C);
  and and_3 (and_3_out, B, not_5_out);
  not not_5 (not_5_out, D);
  and and_4 (and_4_out, A, not_6_out);
  not not_6 (not_6_out, B);
  and and_5 (and_5_out, A, C);
  or or_1 (x, and_1_out, and_2_out, and_3_out, and_4_out, and_5_out);
endmodule

module saida_g (
  input  A,
  input  B,
  input  C,
  input  D,
  output x
);

  wire and_1_out, and_2_out, and_3_out, and_4_out, and_5_out, not_1_out, not_2_out, not_3_out, not_4_out,
       not_5_out;

  not not_1 (not_1_out, B);
  and and_1 (and_1_out, not_1_out, C);
  and and_2 (and_2_out, C, not_2_out);
  not not_2 (not_2_out, D);
  not not_3 (not_3_out, A);
  and and_3 (and_3_out, not_3_out, B, not_4_out);
  not not_4 (not_4_out, C);
  and and_4 (and_4_out, A, not_5_out);
  not not_5 (not_5_out, B);
  and and_5 (and_5_out, A, D);
  or or_1 (x, and_1_out, and_2_out, and_3_out, and_4_out, and_5_out);
endmodule
