// Logisim project Componente_3_XOR.circ as structural Verilog: 1 circuit, main circuit main
module main (
  input  A0,
  input  A1,
  output Saida
);

  wire and_1_out, and_2_out, not_1_out, not_2_out;

  not not_1 (not_1_out, A0);
  and and_1 (and_1_out, not_1_out, A1);
  and and_2 (and_2_out, A0, not_2_out);
  not not_2 (not_2_out, A1);
  or or_1 (Saida, and_1_out, and_2_out);

  // Notes on the sheet:
  //   Porta XOR
endmodule
