// Logisim project componente_4_somador_c_4.circ as structural Verilog: 2 circuits, main circuit main
module main (
  input  [7:0] in_1,
  output bit_do_overflow,
  output [7:0] out_3
);

  wire soamador_bit_bit_2_numero_que_sobe, soamador_bit_bit_3_numero_que_sobe,
       soamador_bit_bit_5_numero_que_sobe, soamador_bit_bit_6_numero_que_sobe,
       soamador_bit_bit_7_numero_que_sobe, soamador_bit_bit_8_numero_que_sobe;

  soamador_bit_bit soamador_bit_bit_1 (
    .A1(in_1[7]), .A0(1'b0), .Resto(soamador_bit_bit_2_numero_que_sobe), .Soma_do_bit(out_3[7]),
    .numero_que_sobe(bit_do_overflow));
  soamador_bit_bit soamador_bit_bit_2 (
    .A1(in_1[6]), .A0(1'b0), .Resto(soamador_bit_bit_3_numero_que_sobe), .Soma_do_bit(out_3[6]),
    .numero_que_sobe(soamador_bit_bit_2_numero_que_sobe));
  soamador_bit_bit soamador_bit_bit_3 (
    .A1(in_1[5]), .A0(1'b0), .Resto(out_3[4]), .Soma_do_bit(out_3[5]),
    .numero_que_sobe(soamador_bit_bit_3_numero_que_sobe));
  soamador_bit_bit soamador_bit_bit_4 (
    .A1(in_1[4]), .A0(1'b0), .Resto(soamador_bit_bit_5_numero_que_sobe), .Soma_do_bit(out_3[4]),
    .numero_que_sobe(out_3[4]));
  soamador_bit_bit soamador_bit_bit_5 (
    .A1(in_1[3]), .A0(1'b0), .Resto(soamador_bit_bit_6_numero_que_sobe), .Soma_do_bit(out_3[3]),
    .numero_que_sobe(soamador_bit_bit_5_numero_que_sobe));
  soamador_bit_bit soamador_bit_bit_6 (
    .A1(in_1[2]), .A0(1'b1), .Resto(soamador_bit_bit_7_numero_que_sobe), .Soma_do_bit(out_3[2]),
    .numero_que_sobe(soamador_bit_bit_6_numero_que_sobe));
  soamador_bit_bit soamador_bit_bit_7 (
    .A1(in_1[1]), .A0(1'b0), .Resto(soamador_bit_bit_8_numero_que_sobe), .Soma_do_bit(out_3[1]),
    .numero_que_sobe(soamador_bit_bit_7_numero_que_sobe));
  soamador_bit_bit soamador_bit_bit_8 (
    .A1(in_1[0]), .A0(1'b0), .Resto(1'b0), .Soma_do_bit(out_3[0]),
    .numero_que_sobe(soamador_bit_bit_8_numero_que_sobe));
endmodule

module soamador_bit_bit (
  input  A0,
  input  A1,
  input  Resto,
  output Soma_do_bit,
  output numero_que_sobe
);

  wire and_1_out, and_2_out, and_3_out, xor_1_out;

  xor xor_1 (xor_1_out, A0, A1);
  and and_1 (and_1_out, A0, A1);
  and and_2 (and_2_out, A0, Resto);
  and and_3 (and_3_out, A1, Resto);
  xor xor_2 (Soma_do_bit, xor_1_out, Resto);
  or or_1 (numero_que_sobe, and_1_out, and_2_out, and_3_out);
endmodule
