// Logisim project componente_5_memoria_rom.circ as structural Verilog: 2 circuits, main circuit main
module main (
  input  [7:0] in_1,
  input  [7:0] in_2,
  input  [1:0] seletor,
  input  [7:0] in_4,
  input  [7:0] in_5,
  output [7:0] saida
);

  wire decodificador_a0, decodificador_a1, decodificador_a2, decodificador_a3;

  decodificador decodificador (
    .seletor_2bits(seletor), .A0(decodificador_a0), .A1(decodificador_a1), .A2(decodificador_a2),
    .A3(decodificador_a3));
  assign saida = decodificador_a0 ? in_1 : 8'bz;  // Controlled_Buffer controlled_buffer_1
  assign saida = decodificador_a1 ? in_2 : 8'bz;  // Controlled_Buffer controlled_buffer_2
  assign saida = decodificador_a2 ? in_4 : 8'bz;  // Controlled_Buffer controlled_buffer_3
  assign saida = decodificador_a3 ? in_5 : 8'bz;  // Controlled_Buffer controlled_buffer_4
endmodule

module decodificador (
  input  [1:0] seletor_2bits,
  output A0,
  output A1,
  output A2,
  output A3
);

  wire not_1_out, not_2_out, not_3_out, not_4_out;

  not not_1 (not_1_out, seletor_2bits[1]);
  not not_2 (not_2_out, seletor_2bits[0]);
  not not_3 (not_3_out, seletor_2bits[1]);
  not not_4 (not_4_out, seletor_2bits[0]);
  and and_1 (A0, not_1_out, not_2_out);
  and and_2 (A1, not_3_out, seletor_2bits[0]);
  and and_3 (A2, seletor_2bits[1], not_4_out);
  and and_4 (A3, seletor_2bits[1], seletor_2bits[0]);
endmodule
