// Logisim project componente_6_Memoria_ram.circ as structural Verilog: 4 circuits, main circuit main
module main (
  input  [7:0] Entrada_de_dados,
  input  [1:0] Seletor,
  input  WE,
  input  clear,
  input  preset,
  output [7:0] out_6
);

  wire and_1_out, and_2_out, and_3_out, and_4_out, Decodificador_a0, Decodificador_a1, Decodificador_a2,
       Decodificador_a3;
  wire [7:0] _1_s0, _2_s0, _3_s0, _4_s0;

  decodificador Decodificador (
    .Seletor_2_bits(Seletor), .A0(Decodificador_a0), .A1(Decodificador_a1), .A2(Decodificador_a2),
    .A3(Decodificador_a3));
  and and_1 (and_1_out, Decodificador_a0, WE);
  and and_2 (and_2_out, Decodificador_a1, WE);
  and and_3 (and_3_out, Decodificador_a2, WE);
  and and_4 (and_4_out, Decodificador_a3, WE);
  Registrador_8_bits _1 (
    .Entrada(Entrada_de_dados), .Enable_clock(and_1_out), .clear(clear), .preset(preset), .S7(_1_s0[7]),
    .S6(_1_s0[6]), .S5(_1_s0[5]), .S4(_1_s0[4]), .S3(_1_s0[3]), .S2(_1_s0[2]), .S1(_1_s0[1]), .S0(_1_s0[0]));
  Registrador_8_bits _2 (
    .Entrada(Entrada_de_dados), .Enable_clock(and_2_out), .clear(clear), .preset(preset), .S7(_2_s0[7]),
    .S6(_2_s0[6]), .S5(_2_s0[5]), .S4(_2_s0[4]), .S3(_2_s0[3]), .S2(_2_s0[2]), .S1(_2_s0[1]), .S0(_2_s0[0]));
  Registrador_8_bits _3 (
    .Entrada(Entrada_de_dados), .Enable_clock(and_3_out), .clear(clear), .preset(preset), .S7(_3_s0[7]),
    .S6(_3_s0[6]), .S5(_3_s0[5]), .S4(_3_s0[4]), .S3(_3_s0[3]), .S2(_3_s0[2]), .S1(_3_s0[1]), .S0(_3_s0[0]));
  Registrador_8_bits _4 (
    .Entrada(Entrada_de_dados), .Enable_clock(and_4_out), .clear(clear), .preset(preset), .S7(_4_s0[7]),
    .S6(_4_s0[6]), .S5(_4_s0[5]), .S4(_4_s0[4]), .S3(_4_s0[3]), .S2(_4_s0[2]), .S1(_4_s0[1]), .S0(_4_s0[0]));
  assign out_6 = Decodificador_a0 ? _1_s0 : 8'bz;  // Controlled_Buffer controlled_buffer_1
  assign out_6 = Decodificador_a1 ? _2_s0 : 8'bz;  // Controlled_Buffer controlled_buffer_2
  assign out_6 = Decodificador_a2 ? _3_s0 : 8'bz;  // Controlled_Buffer controlled_buffer_3
  assign out_6 = Decodificador_a3 ? _4_s0 : 8'bz;  // Controlled_Buffer controlled_buffer_4

  // Notes on the sheet:
  //   MEMORIA RAM 
endmodule

// Registrador
module Registrador_8_bits (
  input  clear,
  input  preset,
  input  [7:0] Entrada,
  input  Enable_clock,
  output S7,
  output S6,
  output S5,
  output S4,
  output S3,
  output S2,
  output S1,
  output S0
);

  flip_flop_tipo_D flip_flop_tipo_d_1 (
    .in_2(Entrada[7]), .preset(preset), .enable_clock(Enable_clock), .clear(clear), .out_5(S7));  // open: out_6
  flip_flop_tipo_D flip_flop_tipo_d_2 (
    .in_2(Entrada[6]), .preset(preset), .enable_clock(Enable_clock), .clear(clear), .out_5(S6));  // open: out_6
  flip_flop_tipo_D flip_flop_tipo_d_3 (
    .in_2(Entrada[4]), .preset(preset), .enable_clock(Enable_clock), .clear(clear), .out_5(S4));  // open: out_6
  flip_flop_tipo_D flip_flop_tipo_d_4 (
    .in_2(Entrada[5]), .preset(preset), .enable_clock(Enable_clock), .clear(clear), .out_5(S5));  // open: out_6
  flip_flop_tipo_D flip_flop_tipo_d_5 (
    .in_2(Entrada[3]), .preset(preset), .enable_clock(Enable_clock), .clear(clear), .out_5(S3));  // open: out_6
  flip_flop_tipo_D flip_flop_tipo_d_6 (
    .in_2(Entrada[1]), .preset(preset), .enable_clock(Enable_clock), .clear(clear), .out_5(S1));  // open: out_6
  flip_flop_tipo_D flip_flop_tipo_d_7 (
    .in_2(Entrada[2]), .preset(preset), .enable_clock(Enable_clock), .clear(clear), .out_5(S2));  // open: out_6
  flip_flop_tipo_D flip_flop_tipo_d_8 (
    .in_2(Entrada[0]), .preset(preset), .enable_clock(Enable_clock), .clear(clear), .out_5(S0));  // open: out_6
endmodule

module decodificador (
  input  [1:0] Seletor_2_bits,
  output A0,
  output A1,
  output A2,
  output A3
);

  wire not_1_out, not_2_out, not_3_out, not_4_out;

  not not_1 (not_1_out, Seletor_2_bits[0]);
  not not_2 (not_2_out, Seletor_2_bits[1]);
  not not_3 (not_3_out, Seletor_2_bits[1]);
  not not_4 (not_4_out, Seletor_2_bits[0]);
  and and_1 (A0, not_1_out, not_2_out);
  and and_2 (A1, Seletor_2_bits[0], not_3_out);
  and and_3 (A2, not_4_out, Seletor_2_bits[1]);
  and and_4 (A3, Seletor_2_bits[0], Seletor_2_bits[1]);
endmodule

module flip_flop_tipo_D (
  input  preset,
  input  in_2,
  input  enable_clock,
  input  clear,
  output out_5,
  output out_6
);

  wire nand_1_out, nand_2_out, nand_3_out, nand_4_out, nand_5_out, nand_6_out, not_1_out, not_2_out,
       not_3_out, not_4_out;

  not not_1 (not_1_out, in_2);
  nand nand_1 (nand_1_out, in_2, enable_clock);
  nand nand_2 (nand_2_out, enable_clock, not_1_out);
  not not_2 (not_2_out, enable_clock);
  nand nand_3 (nand_3_out, not_3_out, nand_1_out, nand_4_out);
  nand nand_4 (nand_4_out, nand_3_out, nand_2_out, not_4_out);
  not not_3 (not_3_out, preset);
  nand nand_5 (nand_5_out, nand_3_out, not_4_out, not_2_out);
  nand nand_6 (nand_6_out, not_2_out, not_3_out, nand_4_out);
  not not_4 (not_4_out, clear);
  nand nand_7 (out_5, nand_5_out, not_3_out, out_6);
  nand nand_8 (out_6, out_5, not_4_out, nand_6_out);

  // Notes on the sheet:
  //   FLIP FLOP TIPO D
endmodule
