// Logisim project Componente07_BancoDeRegs.circ as structural Verilog: 5 circuits, main circuit main
module main (
  input  [1:0] in_1,
  input  [1:0] clear,
  input  Presset_ALL,
  input  [1:0] Escrita,
  input  [7:0] in_5,
  output [7:0] out_6
);

  wire decodificador_2_bits_1_out_2, decodificador_2_bits_1_out_3, decodificador_2_bits_1_out_4,
       decodificador_2_bits_1_out_5, decodificador_2_bits_2_out_2, decodificador_2_bits_2_out_3,
       decodificador_2_bits_2_out_4, decodificador_2_bits_2_out_5;
  wire [7:0] registrador_1_out_5, registrador_2_out_5, registrador_3_out_5, registrador_4_out_5;

  Registrador registrador_1 (
    .Preset(Presset_ALL), .Enable(decodificador_2_bits_1_out_5), .Clear(decodificador_2_bits_2_out_5),
    .in_4(in_5), .out_5(registrador_1_out_5));
  Registrador registrador_2 (
    .Preset(Presset_ALL), .Enable(decodificador_2_bits_1_out_4), .Clear(decodificador_2_bits_2_out_4),
    .in_4(in_5), .out_5(registrador_2_out_5));
  Registrador registrador_3 (
    .Preset(Presset_ALL), .Enable(decodificador_2_bits_1_out_3), .Clear(decodificador_2_bits_2_out_3),
    .in_4(in_5), .out_5(registrador_3_out_5));
  Decodificador_2_bits decodificador_2_bits_1 (
    .in_1(Escrita), .out_2(decodificador_2_bits_1_out_2), .out_3(decodificador_2_bits_1_out_3),
    .out_4(decodificador_2_bits_1_out_4), .out_5(decodificador_2_bits_1_out_5));
  Registrador registrador_4 (
    .Preset(Presset_ALL), .Enable(decodificador_2_bits_1_out_2), .Clear(decodificador_2_bits_2_out_2),
    .in_4(in_5), .out_5(registrador_4_out_5));
  MUX_4_1 mux_4_1_1 (
    .in_1(in_1), .A(registrador_4_out_5), .B(registrador_3_out_5), .C(registrador_2_out_5),
    .D(registrador_1_out_5), .out_6(out_6));
  Decodificador_2_bits decodificador_2_bits_2 (
    .in_1(clear), .out_2(decodificador_2_bits_2_out_2), .out_3(decodificador_2_bits_2_out_3),
    .out_4(decodificador_2_bits_2_out_4), .out_5(decodificador_2_bits_2_out_5));

  // Notes on the sheet:
  //   /
  //   Enable
  //   Mostrar qual dos registradores tem algo
endmodule

module Flip_Flop_D (
  input  Preset,
  input  Data,
  input  Enable,
  input  Clear,
  output out_5
);

  wire nand_1_out, nand_2_out, nand_3_out, nand_4_out, nand_5_out, nand_6_out, nand_8_out, not_1_out,
       not_2_out;

  nand nand_1 (nand_1_out, Data, Enable);
  nand nand_2 (nand_2_out, ~Data, Enable);  // NAND_Gate
  nand nand_3 (nand_3_out, not_1_out, nand_1_out, nand_4_out);
  nand nand_4 (nand_4_out, nand_3_out, nand_2_out, not_2_out);
  nand nand_5 (nand_5_out, nand_3_out, not_2_out, Enable);
  nand nand_6 (nand_6_out, Enable, not_1_out, nand_4_out);
  not not_1 (not_1_out, Preset);
  nand nand_7 (out_5, not_1_out, nand_5_out, nand_8_out);
  nand nand_8 (nand_8_out, out_5, nand_6_out, not_2_out);
  not not_2 (not_2_out, Clear);
endmodule

module Registrador (
  input  Preset,
  input  Enable,
  input  Clear,
  input  [7:0] in_4,
  output [7:0] out_5
);

  Flip_Flop_D ff_d_1 (.Preset(Preset), .Data(in_4[7]), .out_5(out_5[7]), .Enable(Enable), .Clear(Clear));
  Flip_Flop_D ff_d_2 (.Preset(Preset), .Data(in_4[6]), .out_5(out_5[6]), .Enable(Enable), .Clear(Clear));
  Flip_Flop_D ff_d_3 (.Preset(Preset), .Data(in_4[5]), .out_5(out_5[5]), .Enable(Enable), .Clear(Clear));
  Flip_Flop_D ff_d_4 (.Preset(Preset), .Data(in_4[4]), .out_5(out_5[4]), .Enable(Enable), .Clear(Clear));
  Flip_Flop_D ff_d_5 (.Preset(Preset), .Data(in_4[3]), .out_5(out_5[3]), .Enable(Enable), .Clear(Clear));
  Flip_Flop_D ff_d_6 (.Preset(Preset), .Data(in_4[2]), .out_5(out_5[2]), .Enable(Enable), .Clear(Clear));
  Flip_Flop_D ff_d_7 (.Preset(Preset), .Data(in_4[1]), .out_5(out_5[1]), .Enable(Enable), .Clear(Clear));
  Flip_Flop_D ff_d_8 (.Preset(Preset), .Data(in_4[0]), .out_5(out_5[0]), .Enable(Enable), .Clear(Clear));
endmodule

module MUX_4_1 (
  input  [1:0] in_1,
  input  [7:0] A,
  input  [7:0] B,
  input  [7:0] C,
  input  [7:0] D,
  output [7:0] out_6
);

  wire decodificador_2_bits_1_out_2, decodificador_2_bits_1_out_3, decodificador_2_bits_1_out_4,
       decodificador_2_bits_1_out_5;

  Decodificador_2_bits decodificador_2_bits_1 (
    .in_1(in_1), .out_2(decodificador_2_bits_1_out_2), .out_3(decodificador_2_bits_1_out_3),
    .out_4(decodificador_2_bits_1_out_4), .out_5(decodificador_2_bits_1_out_5));
  assign out_6 = decodificador_2_bits_1_out_5 ? D : 8'bz;  // Controlled_Buffer controlled_buffer_1
  assign out_6 = decodificador_2_bits_1_out_2 ? A : 8'bz;  // Controlled_Buffer controlled_buffer_2
  assign out_6 = decodificador_2_bits_1_out_3 ? B : 8'bz;  // Controlled_Buffer controlled_buffer_3
  assign out_6 = decodificador_2_bits_1_out_4 ? C : 8'bz;  // Controlled_Buffer controlled_buffer_4
endmodule

module Decodificador_2_bits (
  input  [1:0] in_1,
  output out_2,
  output out_3,
  output out_4,
  output out_5
);

  and and_1 (out_2, ~in_1[0], ~in_1[1]);  // AND_Gate
  and and_2 (out_3, in_1[0], ~in_1[1]);  // AND_Gate
  and and_3 (out_4, ~in_1[0], in_1[1]);  // AND_Gate
  and and_4 (out_5, in_1[0], in_1[1]);
endmodule
