// Logisim project componente_8_Somador-8bits.circ as structural Verilog
module somador (
  input  A0,
  input  A1,
  input  Resto,
  output Soma_do_bit,
  output Numero_que_sobe
);

  wire and_1_out, and_2_out, and_3_out, xor_1_out;

  xor xor_1 (xor_1_out, A0, A1);
  and and_1 (and_1_out, A0, A1);
  and and_2 (and_2_out, A0, Resto);
  and and_3 (and_3_out, A1, Resto);
  xor xor_2 (Soma_do_bit, xor_1_out, Resto);
  or or_1 (Numero_que_sobe, and_1_out, and_2_out, and_3_out);
endmodule

module somador8bits (
  input  [7:0] in_1,
  input  [7:0] in_2,
  output [7:0] out_3,
  output OverFlow
);

  wire somador_1_numero_que_sobe, somador_2_numero_que_sobe, somador_3_numero_que_sobe,
       somador_4_numero_que_sobe, somador_5_numero_que_sobe, somador_6_numero_que_sobe,
       somador_7_numero_que_sobe;

  somador somador_1 (
    .A1(in_2[0]), .A0(in_1[0]), .Resto(1'b0), .Soma_do_bit(out_3[0]),
    .Numero_que_sobe(somador_1_numero_que_sobe));
  somador somador_2 (
    .A1(in_2[1]), .A0(in_1[1]), .Resto(somador_1_numero_que_sobe), .Soma_do_bit(out_3[1]),
    .Numero_que_sobe(somador_2_numero_que_sobe));
  somador somador_3 (
    .A1(in_2[2]), .A0(in_1[2]), .Resto(somador_2_numero_que_sobe), .Soma_do_bit(out_3[2]),
    .Numero_que_sobe(somador_3_numero_que_sobe));
  somador somador_4 (
    .A1(in_2[3]), .A0(in_1[3]), .Resto(somador_3_numero_que_sobe), .Soma_do_bit(out_3[3]),
    .Numero_que_sobe(somador_4_numero_que_sobe));
  somador somador_5 (
    .A1(in_2[4]), .A0(in_1[4]), .Resto(somador_4_numero_que_sobe), .Soma_do_bit(out_3[4]),
    .Numero_que_sobe(somador_5_numero_que_sobe));
  somador somador_6 (
    .A1(in_2[5]), .A0(in_1[5]), .Resto(somador_5_numero_que_sobe), .Soma_do_bit(out_3[5]),
    .Numero_que_sobe(somador_6_numero_que_sobe));
  somador somador_7 (
    .A1(in_2[6]), .A0(in_1[6]), .Resto(somador_6_numero_que_sobe), .Soma_do_bit(out_3[6]),
    .Numero_que_sobe(somador_7_numero_que_sobe));
  somador somador_8 (
    .A1(in_2[7]), .A0(in_1[7]), .Resto(somador_7_numero_que_sobe), .Soma_do_bit(out_3[7]),
    .Numero_que_sobe(OverFlow));
endmodule
